# Fritzing sketch Nixie (saved by Fritzing 0.9.4)
circuit board: 17.7cm x 8.3cm
breadboards: 1

parts:
  R4 = Resistor [tolerance=±5% resistance=10M package=THT]
  R5 = Resistor [tolerance=±5% resistance=330k package=THT]
  R6 = Resistor [tolerance=±20% resistance=100k package=THT]
  R7 = Resistor [tolerance=±20% resistance=100k package=THT]
  R8 = Resistor [tolerance=±20% resistance=100k package=THT]
  R9 = Resistor [tolerance=±20% resistance=100k package=THT]
  R10 = Resistor [tolerance=±20% resistance=100k package=THT]
  R11 = Resistor [tolerance=±20% resistance=100k package=THT]
  R12 = Resistor [tolerance=±20% resistance=100k package=THT]
  R13 = Resistor [tolerance=±20% resistance=100k package=THT]
  R14 = Resistor [tolerance=±20% resistance=100k package=THT]
  Q1 = NPN-Transistor [part_number=BC547 package="TO92 [THT]"]
  Q2 = NPN-Transistor [part_number=BC547 package="TO92 [THT]"]
  R15 = Resistor [tolerance=±5% resistance=2.2M package=THT]
  R16 = Resistor [tolerance=±5% resistance=2.2M package=THT]
  Q3 = NPN-Transistor [part_number=MPSA42 package="TO92 [THT]"]
  R17 = Resistor [tolerance=±5% resistance=33k package=THT]
  Q4 = NPN-Transistor [part_number=MPSA42 package="TO92 [THT]"]
  R18 = Resistor [tolerance=±5% resistance=33k package=THT]
  Q5 = NPN-Transistor [part_number=MPSA42 package="TO92 [THT]"]
  Q6 = NPN-Transistor [part_number=MPSA42 package="TO92 [THT]"]
  R19 = Resistor [tolerance=±5% resistance=33k package=THT]
  R20 = Resistor [tolerance=±5% resistance=33k package=THT]
  Q7 = NPN-Transistor [part_number=MPSA42 package="TO92 [THT]"]
  Q8 = NPN-Transistor [part_number=MPSA42 package="TO92 [THT]"]
  R21 = Resistor [tolerance=±5% resistance=33k package=THT]
  R22 = Resistor [tolerance=±5% resistance=33k package=THT]
  Q9 = NPN-Transistor [part_number=MPSA42 package="TO92 [THT]"]
  Q10 = NPN-Transistor [part_number=MPSA42 package="TO92 [THT]"]
  R23 = Resistor [tolerance=±5% resistance=33k package=THT]
  R24 = Resistor [tolerance=±5% resistance=33k package=THT]
  Q11 = NPN-Transistor [part_number=MPSA42 package="TO92 [THT]"]
  Q12 = NPN-Transistor [part_number=MPSA42 package="TO92 [THT]"]
  R25 = Resistor [tolerance=±5% resistance=33k package=THT]
  R26 = Resistor [tolerance=±5% resistance=33k package=THT]
  Q13 = NPN-Transistor [part_number=MPSA42 package="TO92 [THT]"]
  Q14 = NPN-Transistor [part_number=MPSA42 package="TO92 [THT]"]
  Q15 = NPN-Transistor [part_number=MPSA42 package="TO92 [THT]"]
  Q16 = NPN-Transistor [part_number=MPSA42 package="TO92 [THT]"]
  Q17 = NPN-Transistor [part_number=MPSA42 package="TO92 [THT]"]
  Q18 = NPN-Transistor [part_number=MPSA42 package="TO92 [THT]"]
  R27 = Resistor [tolerance=±5% resistance=33k package=THT]
  R28 = Resistor [tolerance=±5% resistance=33k package=THT]
  R29 = Resistor [tolerance=±5% resistance=33k package=THT]
  R30 = Resistor [tolerance=±5% resistance=33k package=THT]
  R31 = Resistor [tolerance=±5% resistance=33k package=THT]
  R32 = Resistor [tolerance=±5% resistance=33k package=THT]
  R33 = Resistor [tolerance=±5% resistance=33k package=THT]
  R34 = Resistor [tolerance=±5% resistance=33k package=THT]
  Q19 = NPN-Transistor [part_number=MPSA42 package="TO92 [THT]"]
  Q20 = NPN-Transistor [part_number=MPSA42 package="TO92 [THT]"]
  Q21 = NPN-Transistor [part_number=MPSA42 package="TO92 [THT]"]
  Q22 = NPN-Transistor [part_number=MPSA42 package="TO92 [THT]"]
  Q23 = NPN-Transistor [part_number=MPSA42 package="TO92 [THT]"]
  Q24 = NPN-Transistor [part_number=MPSA42 package="TO92 [THT]"]
  Q25 = NPN-Transistor [part_number=MPSA42 package="TO92 [THT]"]
  Q26 = NPN-Transistor [part_number=MPSA42 package="TO92 [THT]"]
  Q27 = NPN-Transistor [part_number=MPSA42 package="TO92 [THT]"]
  Q28 = NPN-Transistor [part_number=MPSA42 package="TO92 [THT]"]
  Q29 = NPN-Transistor [part_number=MPSA42 package="TO92 [THT]"]
  Q30 = NPN-Transistor [part_number=MPSA42 package="TO92 [THT]"]
  Q31 = NPN-Transistor [part_number=MPSA42 package="TO92 [THT]"]
  Q32 = NPN-Transistor [part_number=MPSA42 package="TO92 [THT]"]
  Q33 = NPN-Transistor [part_number=MPSA42 package="TO92 [THT]"]
  Q34 = NPN-Transistor [part_number=MPSA42 package="TO92 [THT]"]
  R35 = Resistor [tolerance=±5% resistance=33k package=THT]
  R36 = Resistor [tolerance=±5% resistance=33k package=THT]
  R37 = Resistor [tolerance=±5% resistance=33k package=THT]
  R38 = Resistor [tolerance=±5% resistance=33k package=THT]
  R39 = Resistor [tolerance=±5% resistance=33k package=THT]
  R40 = Resistor [tolerance=±5% resistance=33k package=THT]
  R41 = Resistor [tolerance=±5% resistance=33k package=THT]
  R42 = Resistor [tolerance=±5% resistance=33k package=THT]
  R43 = Resistor [tolerance=±5% resistance=33k package=THT]
  R44 = Resistor [tolerance=±5% resistance=33k package=THT]
  R45 = Resistor [tolerance=±5% resistance=33k package=THT]
  R46 = Resistor [tolerance=±5% resistance=33k package=THT]
  R47 = Resistor [tolerance=±5% resistance=33k package=THT]
  R48 = Resistor [tolerance=±5% resistance=33k package=THT]
  R49 = Resistor [tolerance=±5% resistance=33k package=THT]
  R50 = Resistor [tolerance=±5% resistance=33k package=THT]
  R51 = Resistor [tolerance=±5% resistance=33k package=THT]
  R52 = Resistor [tolerance=±5% resistance=33k package=THT]
  Q35 = NPN-Transistor [part_number=MPSA42 package="TO92 [THT]"]
  Q36 = NPN-Transistor [part_number=MPSA42 package="TO92 [THT]"]
  Q37 = NPN-Transistor [part_number=MPSA42 package="TO92 [THT]"]
  Q38 = NPN-Transistor [part_number=MPSA42 package="TO92 [THT]"]
  Q39 = NPN-Transistor [part_number=MPSA42 package="TO92 [THT]"]
  Q40 = NPN-Transistor [part_number=MPSA42 package="TO92 [THT]"]
  Q42 = NPN-Transistor [part_number=MPSA42 package="TO92 [THT]"]
  Q43 = NPN-Transistor [part_number=MPSA42 package="TO92 [THT]"]
  Q44 = NPN-Transistor [part_number=MPSA42 package="TO92 [THT]"]
  Q45 = NPN-Transistor [part_number=MPSA42 package="TO92 [THT]"]
  Q46 = NPN-Transistor [part_number=MPSA42 package="TO92 [THT]"]
  Q47 = NPN-Transistor [part_number=MPSA42 package="TO92 [THT]"]
  Q50 = NPN-Transistor [part_number=MPSA42 package="TO92 [THT]"]
  R53 = Resistor [tolerance=±5% resistance=33k package=THT]
  R54 = Resistor [tolerance=±5% resistance=33k package=THT]
  R55 = Resistor [tolerance=±5% resistance=33k package=THT]
  R56 = Resistor [tolerance=±5% resistance=33k package=THT]
  R57 = Resistor [tolerance=±5% resistance=33k package=THT]
  R58 = Resistor [tolerance=±5% resistance=33k package=THT]
  R59 = Resistor [tolerance=±5% resistance=33k package=THT]
  R60 = Resistor [tolerance=±5% resistance=33k package=THT]
  R61 = Resistor [tolerance=±5% resistance=33k package=THT]
  R62 = Resistor [tolerance=±5% resistance=33k package=THT]
  R63 = Resistor [tolerance=±5% resistance=33k package=THT]
  R66 = Resistor [tolerance=±5% resistance=33k package=THT]
  R68 = Resistor [tolerance=±5% resistance=33k package=THT]
  R69 = Resistor [tolerance=±5% resistance=33k package=THT]
  R70 = Resistor [tolerance=±5% resistance=68k package=THT]
  XTAL1 = CRYSTAL - kHz [frequency="32 kHz"]
  HVPS = HVPS1364
  C3 = Ceramic Capacitor [capacitance=100nF voltage=250V package="200 mil [THT, multilayer]"]
  RGB-CTRL = RGV CONTROLLER
  Q51 = PNP-Transistor [package="TO92 [THT]"]
  Q52 = PNP-Transistor [package="TO92 [THT]"]
  Q53 = PNP-Transistor [package="TO92 [THT]"]
  R72 = Resistor [tolerance=±5% resistance=1k package=THT]
  R73 = Resistor [tolerance=±5% resistance=1k package=THT]
  R74 = Resistor [tolerance=±5% resistance=1k package=THT]
  R75 = Resistor [tolerance=±5% resistance=1k package=THT]
  R76 = Resistor [tolerance=±5% resistance=1k package=THT]
  R77 = Resistor [tolerance=±5% resistance=47 package=THT]
  D14 = Diode [package=diode-1n4148]
  D15 = Diode [package=diode-1n4148]
  D13 = Diode [package=diode-1n4148]
  D18 = Diode [package=diode-1n4148]
  D17 = Diode [package=diode-1n4148]
  D19 = Diode [package=diode-1n4148]
  D20 = Diode [package=diode-1n4148]
  D21 = Diode [package=diode-1n4148]
  D22 = Diode [package=diode-1n4148]
  D23 = Diode [package=diode-1n4148]
  D24 = Diode [package=diode-1n4148]
  D25 = Diode [package=diode-1n4148]
  D27 = Diode [package=diode-1n4148]
  D26 = Diode [package=diode-1n4148]
  U1 = 555 Timer [package="DIP8 [THT]"]
  R78 = Resistor [tolerance=±5% resistance=1M package=THT]
  C8 = Electrolytic Capacitor [capacitance=10µF package="100 mil [THT, electrolytic]"]
  R79 = Resistor [tolerance=±5% resistance=100k package=THT]
  R80 = Resistor [tolerance=±5% resistance=100k package=THT]
  S2 = double row female pin header, 16 pins [form="♀ (female)"]
  C4 = Ceramic Capacitor [capacitance=100nF package="200 mil [THT, multilayer]"]
  H2 = double row female pin header, 16 pins [form="♀ (female)"]
  M2 = double row female pin header, 16 pins [form="♀ (female)"]
  M1 = double row female pin header, 16 pins [form="♀ (female)"]
  D16 = Diode [package=diode-1n4148]
  S1 = double row female pin header, 16 pins [form="♀ (female)"]
  H1 = double row female pin header, 16 pins [form="♀ (female)"]
  C2 = Ceramic Capacitor [capacitance=15pF voltage=6.3V package="200 mil [THT, multilayer]"]
  C1 = Ceramic Capacitor [capacitance=15pF voltage=6.3V package="200 mil [THT, multilayer]"]
  J1 = Screw terminal - 2 pins [package=THT]
  INTERFACE = female pin header, 5 pins [form="♀ (female)"]
  J2 = female pin header, 1 pin [form="♀ (female)"]
  CD4017 = CD4017 - Decade Counter [chip_label=CD4017 package="DIP (Dual Inline) [THT]"]
  CD4017_2 = CD4017 - Decade Counter [chip_label=CD4017 package="DIP (Dual Inline) [THT]"]
  CD4017_3 = CD4017 - Decade Counter [chip_label=CD4017 package="DIP (Dual Inline) [THT]"]
  CD4017_4 = CD4017 - Decade Counter [chip_label=CD4017 package="DIP (Dual Inline) [THT]"]
  CD4017_5 = CD4017 - Decade Counter [chip_label=CD4017 package="DIP (Dual Inline) [THT]"]
  CD4013 = CD4013 Dual D-Type Flip-Flop [chip_label=CD4013 package="DIP (Dual Inline) [THT]"]
  CD4060 = CD4060 - 14-Stage Ripple Carry Binary Counter [chip_label=CD4060 package="DIP (Dual Inline) [THT]"]
  D28 = Diode [package=diode-1n4148]
  R81 = Resistor [tolerance=±5% resistance=100k package=THT]
  R82 = Resistor [tolerance=±5% resistance=100k package=THT]
  C9 = Electrolytic Capacitor [capacitance=10µF package="100 mil [THT, electrolytic]"]
  Q54 = NPN-Transistor [part_number=MPSA42 package="TO92 [THT]"]
  R83 = Resistor [tolerance=±5% resistance=33k package=THT]
  R84 = Resistor [tolerance=±5% resistance=150k package=THT]
  R85 = Resistor [tolerance=±5% resistance=150k package=THT]
  Q55 = NPN-Transistor [part_number=MPSA42 package="TO92 [THT]"]
  R86 = Resistor [tolerance=±5% resistance=33k package=THT]
  R87 = Resistor [tolerance=±5% resistance=39k package=THT]
  C10 = Ceramic Capacitor [capacitance=10nF package="200 mil [THT, multilayer]"]
  CD4017_6 = CD4017 - Decade Counter [chip_label=CD4017 package="DIP (Dual Inline) [THT]"]

nets (from the pcb view):
  N1: R4.Pin_0, XTAL1.pin_0, C1.1, CD4060.P1
  N2: R4.Pin_1, R5.Pin_1, CD4060./P0
  N3: R5.Pin_0, XTAL1.pin_1, C2.1
  VSS: R6.Pin_0, R7.Pin_0, R8.Pin_0, R9.Pin_0, R10.Pin_0, R11.Pin_0, R12.Pin_0, R13.Pin_0, R14.Pin_0, Q3.E, Q4.E, Q5.E, Q6.E, Q7.E, Q8.E, Q9.E, Q10.E, Q11.E, Q12.E, Q13.E, Q14.E, Q15.E, Q16.E, Q17.E, Q18.E, Q19.E, Q20.E, Q21.E, Q22.E, Q23.E, Q24.E, Q25.E, Q26.E, Q27.E, Q28.E, Q29.E, Q30.E, Q31.E, Q32.E, Q33.E, Q34.E, Q35.E, Q36.E, Q37.E, Q38.E, Q39.E, Q40.E, Q42.E, Q43.E, Q44.E, Q45.E, Q46.E, Q47.E, Q50.E, HVPS.GND, C3.0, RGB-CTRL.GND, U1.Ground, C8.-, R79.Pin_0, C4.0, C2.0, C1.0, J1.pin1, INTERFACE.pin1, CD4017.VSS, CD4017.ENA, CD4017_2.VSS, CD4017_2.ENA, CD4017_3.VSS, CD4017_3.ENA, CD4017_4.VSS, CD4017_4.ENA, CD4017_5.VSS, CD4017_5.ENA, CD4013.RESET1, CD4013.SET1, CD4013.VSS, CD4013.SET2, CD4013.DATA2, CD4013.RESET2, CD4013.CLOCK2, CD4060.VSS, CD4060.RESET, R81.Pin_1, R82.Pin_1, Q54.E, Q55.E, R87.Pin_1, C10.0, CD4017_6.VSS, CD4017_6.ENA
  N4: R6.Pin_1, D16.C, CD4017_5.RESET
  N5: R7.Pin_1, R61.Pin_0, R68.Pin_0, D17.C, J2.pin1, CD4017_5.CLOCK
  N6: R8.Pin_1, D18.C, D19.C, CD4017_4.RESET
  N7: R9.Pin_1, D22.C, D23.C, CD4017_2.RESET
  N8: R10.Pin_1, D20.C, INTERFACE.pin4, CD4017_3.CLOCK
  N9: R11.Pin_1, D21.C, CD4017_3.RESET
  N10: R12.Pin_1, D27.C, D26.C, CD4017.RESET
  N11: R13.Pin_1, D24.C, INTERFACE.pin5, CD4017_6.CLOCK
  N12: R14.Pin_1, D25.C, CD4017_6.RESET
  N13: Q1.E, Q2.C
  N14: Q1.B, R15.Pin_0
  VDD: Q1.C, HVPS.VIN, RGB-CTRL.VIN, Q51.E, Q52.E, Q53.E, U1.Reset, U1.Vcc_Supply_Voltage, R78.Pin_1, R80.Pin_1, C4.1, J1.pin2, INTERFACE.pin2, CD4017.VDD, CD4017_2.VDD, CD4017_3.VDD, CD4017_4.VDD, CD4017_5.VDD, CD4013.VDD, CD4060.VDD, C9.+, CD4017_6.VDD
  N15: Q2.E, D18.A, D21.A, D22.A, D25.A, D26.A, D16.A, D28.C, R81.Pin_0
  N16: Q2.B, R16.Pin_0
  N17: R15.Pin_1, R55.Pin_0, CD4017.Q2
  N18: R16.Pin_1, R66.Pin_0, CD4017_6.Q4
  N19: Q3.B, R17.Pin_1
  N20: Q3.C, S2.pin1
  N21: R17.Pin_0, CD4017_4.Q1
  N22: Q4.B, R18.Pin_1
  N23: Q4.C, S2.pin15
  N24: R18.Pin_0, CD4017_4.Q2
  N25: Q5.B, R19.Pin_1
  N26: Q5.C, S2.pin2
  N27: Q6.B, R20.Pin_1
  N28: Q6.C, S2.pin14
  N29: R19.Pin_0, CD4017_4.Q3
  N30: R20.Pin_0, CD4017_4.Q4
  N31: Q7.B, R21.Pin_1
  N32: Q7.C, S2.pin3
  N33: Q8.B, R22.Pin_1
  N34: Q8.C, S1.pin16
  N35: R21.Pin_0, CD4017_4.Q5
  N36: R22.Pin_0, CD4017_5.Q0
  N37: Q9.B, R23.Pin_1
  N38: Q9.C, S1.pin1
  N39: Q10.B, R24.Pin_1
  N40: Q10.C, S1.pin15
  N41: R23.Pin_0, CD4017_5.Q1
  N42: R24.Pin_0, CD4017_5.Q2
  N43: Q11.B, R25.Pin_1
  N44: Q11.C, S1.pin2
  N45: Q12.B, R26.Pin_1
  N46: Q12.C, S1.pin14
  N47: R25.Pin_0, CD4017_5.Q3
  N48: R26.Pin_0, CD4017_5.Q4
  N49: Q13.B, R29.Pin_1
  N50: Q13.C, S1.pin4
  N51: Q14.B, R32.Pin_1
  N52: Q14.C, S1.pin12
  N53: Q15.B, R28.Pin_1
  N54: Q15.C, S1.pin13
  N55: Q16.B, R27.Pin_1
  N56: Q16.C, S2.pin16
  N57: Q17.B, R31.Pin_1
  N58: Q17.C, S1.pin3
  N59: Q18.B, R30.Pin_1
  N60: Q18.C, S1.pin5
  N61: R27.Pin_0, D20.A, CD4017_4.Q0
  N62: R28.Pin_0, CD4017_5.Q6
  N63: R29.Pin_0, CD4017_5.Q7
  N64: R30.Pin_0, CD4017_5.Q9
  N65: R31.Pin_0, CD4017_5.Q5
  N66: R32.Pin_0, CD4017_5.Q8
  N67: R33.Pin_0, S2.pin4, S2.pin13
  N68: R33.Pin_1, R34.Pin_1, R51.Pin_1, R52.Pin_1, R69.Pin_1, R70.Pin_1, HVPS.VOUT, C3.1, R84.Pin_1, R85.Pin_1
  N69: R34.Pin_0, S1.pin6, S1.pin11
  N70: Q19.B, R35.Pin_1
  N71: Q19.C, M2.pin1
  N72: Q20.B, R40.Pin_1
  N73: Q20.C, M1.pin1
  N74: Q21.B, R42.Pin_1
  N75: Q21.C, M1.pin12
  N76: Q22.B, R38.Pin_1
  N77: Q22.C, M1.pin4
  N78: Q23.B, R37.Pin_1
  N79: Q23.C, M2.pin3
  N80: Q24.B, R50.Pin_1
  N81: Q24.C, M1.pin13
  N82: Q25.B, R46.Pin_1
  N83: Q25.C, M2.pin14
  N84: Q26.B, R36.Pin_1
  N85: Q26.C, M2.pin2
  N86: Q27.B, R41.Pin_1
  N87: Q27.C, M1.pin14
  N88: Q28.B, R48.Pin_1
  N89: Q28.C, M2.pin15
  N90: Q29.B, R45.Pin_1
  N91: Q29.C, M1.pin16
  N92: Q30.B, R44.Pin_1
  N93: Q30.C, M1.pin3
  N94: Q31.B, R47.Pin_1
  N95: Q31.C, M1.pin5
  N96: Q32.B, R39.Pin_1
  N97: Q32.C, M2.pin16
  N98: Q33.B, R43.Pin_1
  N99: Q33.C, M1.pin2
  N100: Q34.B, R49.Pin_1
  N101: Q34.C, M1.pin15
  N102: R35.Pin_0, CD4017_2.Q1
  N103: R36.Pin_0, CD4017_2.Q3
  N104: R37.Pin_0, CD4017_2.Q5
  N105: R38.Pin_0, CD4017_3.Q7
  N106: R39.Pin_0, D24.A, CD4017_2.Q0
  N107: R40.Pin_0, CD4017_3.Q1
  N108: R41.Pin_0, CD4017_3.Q4
  N109: R42.Pin_0, CD4017_3.Q8
  N110: R43.Pin_0, CD4017_3.Q3
  N111: R44.Pin_0, CD4017_3.Q5
  N112: R45.Pin_0, CD4017_3.Q0
  N113: R46.Pin_0, CD4017_2.Q4
  N114: R47.Pin_0, CD4017_3.Q9
  N115: R48.Pin_0, CD4017_2.Q2
  N116: R49.Pin_0, CD4017_3.Q2
  N117: R50.Pin_0, CD4017_3.Q6
  N118: R51.Pin_0, M1.pin6, M1.pin11
  N119: R52.Pin_0, M2.pin4, M2.pin13
  N120: Q35.B, R61.Pin_1
  N121: Q35.C, H2.pin5
  N122: Q36.B, R60.Pin_1
  N123: Q36.C, H1.pin3
  N124: Q37.B, R58.Pin_1
  N125: Q37.C, H1.pin13
  N126: Q38.B, R62.Pin_1
  N127: Q38.C, H1.pin15
  N128: Q39.B, R57.Pin_1
  N129: Q39.C, H1.pin2
  N130: Q40.B, R59.Pin_1
  N131: Q40.C, H1.pin4
  N132: Q42.B, R55.Pin_1
  N133: Q42.C, H2.pin15
  N134: Q43.B, R66.Pin_1
  N135: Q43.C, H1.pin14
  N136: Q44.B, R56.Pin_1
  N137: Q44.C, H1.pin5
  N138: Q45.B, R53.Pin_1
  N139: Q45.C, H1.pin12
  N140: Q46.B, R54.Pin_1
  N141: Q46.C, H1.pin1
  N142: Q47.B, R63.Pin_1
  N143: Q47.C, H1.pin16
  N144: Q50.B, R68.Pin_1
  N145: Q50.C, H2.pin6
  N146: R53.Pin_0, CD4017_6.Q8
  N147: R54.Pin_0, CD4017_6.Q1
  N148: R56.Pin_0, CD4017_6.Q9
  N149: R57.Pin_0, CD4017_6.Q3
  N150: R58.Pin_0, CD4017_6.Q6
  N151: R59.Pin_0, CD4017_6.Q7
  N152: R60.Pin_0, CD4017_6.Q5
  N153: R62.Pin_0, CD4017_6.Q2
  N154: R63.Pin_0, CD4017_6.Q0
  N155: R69.Pin_0, H2.pin4, H2.pin13
  N156: R70.Pin_0, H1.pin6, H1.pin11
  N157: HVPS.RADJUST, R87.Pin_0
  N158: HVPS.ENABLE, U1.Output, R79.Pin_1
  N159: RGB-CTRL.B, R74.Pin_1, D15.C
  N160: RGB-CTRL.G, R73.Pin_1, D13.C
  N161: RGB-CTRL.R, R72.Pin_1, D14.C
  N162: Q51.B, R74.Pin_0
  N163: Q51.C, R76.Pin_0
  N164: Q52.B, R73.Pin_0
  N165: Q52.C, R75.Pin_0
  N166: Q53.B, R72.Pin_0
  N167: Q53.C, R77.Pin_0
  N168: R75.Pin_1, S2.pin7, H2.pin7, M2.pin7, M1.pin7, S1.pin7, H1.pin7
  N169: R76.Pin_1, S2.pin10, H2.pin10, M2.pin10, M1.pin10, S1.pin10, H1.pin10
  N170: R77.Pin_1, S2.pin9, H2.pin9, M2.pin9, M1.pin9, S1.pin9, H1.pin9
  N171: D14.A, D15.A, D13.A, S2.pin8, H2.pin8, M2.pin8, M1.pin8, S1.pin8, H1.pin8
  N172: D17.A, CD4013.Q1
  N173: D19.A, CD4017_4.Q6
  N174: D23.A, CD4017_2.Q6
  N175: D27.A, CD4017.Q3
  N176: U1.Trigger, R80.Pin_0, INTERFACE.pin3
  N177: U1.Control_Voltage, C10.1
  N178: U1.Threshold, U1.Discharge, R78.Pin_0, C8.+
  N179: H2.pin1, Q54.C
  N180: H2.pin11, R85.Pin_0
  N181: H2.pin12, R84.Pin_0
  N182: H2.pin16, Q55.C
  N183: CD4017.Q1, R83.Pin_0
  N184: CD4017.Q0, R86.Pin_0
  N185: CD4017.CLOCK, CD4017_6.CO
  N186: CD4017_2.CLOCK, CD4017_3.CO
  N187: CD4017_4.CLOCK, CD4017_5.CO
  N188: CD4013./Q1, CD4013.DATA1
  N189: CD4013.CLOCK1, CD4060.Q14
  N190: D28.A, R82.Pin_0, C9.-
  N191: Q54.B, R83.Pin_1
  N192: Q55.B, R86.Pin_1

notes:
  StrangePlanet (2019)

custom parts:
  CD4017 - Decade Counter: A DIP stand-in part for whatever IC you want. With 16 pins on a 300mil dual inline package (DIP) footprint.
  CD4013 Dual D-Type Flip-Flop: The CD4013B dual D-type flip-flop is a monolithic comple-mentary MOS (CMOS) integrated circuit constructed withN- and P-channel enhancement mode transistors. Eachflip-flop has independent data, set, reset, and clock inputsand “Q” and “Q” outputs. These devices can be used forshift register applications, and by connecting “Q” output tothe data input, for counter and toggle applications.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
